# Fritzing sketch motherboard (saved by Fritzing 0.9.3b)
stripboards: 1

parts:
  IC1 = 6n137 Optocoupler [package="DIP (Dual Inline) [THT]"]
  R1 = Resistor [tolerance=±5% resistance=220 package=THT]
  R2 = Resistor [tolerance=±5% resistance=220 package=THT]
  R3 = Resistor [tolerance=±5% resistance=10k package=THT]
  IC3 = SPEAKJET [package=dil18]
  R4 = Resistor [tolerance=±5% resistance=1k package=THT]
  X1 = SparkFun - microSD Transflash
  D1 = Small signal Diode flat 300mil [part_number=1N4148 package="300 mil [THT]"]
  R7 = Resistor [tolerance=±5% resistance=220 package=THT]
  R8 = Resistor [tolerance=±5% resistance=220 package=THT]
  C4 = Electrolytic Capacitor [capacitance=10µF package="100 mil [THT, electrolytic]"]
  J1 = female pin header, 1 pin [form="♀ (female)"]
  J2 = female pin header, 1 pin [form="♀ (female)"]
  J3 = female pin header, 1 pin [form="♀ (female)"]
  J4 = female pin header, 1 pin [form="♀ (female)"]
  J6 = female pin header, 1 pin [form="♀ (female)"]
  J7 = female pin header, 1 pin [form="♀ (female)"]
  IC4 = TTS256 [package="DIP (Dual Inline) [THT]"]
  U1 = 74x125 [part_number=74x125 package="DIP (Dual Inline) [THT]"]
  U1_3 = 74x125 [part_number=74x125 package="DIP (Dual Inline) [THT]"]  # not connected
  U1_2 = 74x125 [part_number=74x125 package="DIP (Dual Inline) [THT]"]  # not connected
  part = 74x125 [part_number=74x125 package="DIP (Dual Inline) [THT]"]
  U1_1 = 74x125 [part_number=74x125 package="DIP (Dual Inline) [THT]"]
  U1_4 = 74x125 [part_number=74x125 package="DIP (Dual Inline) [THT]"]  # not connected
  J8 = female pin header, 1 pin [form="♀ (female)"]
  J9 = female pin header, 2 pins [form="♀ (female)"]
  J10 = female pin header, 3 pins [form="♀ (female)"]
  J11 = female pin header, 2 pins [form="♀ (female)"]
  J12 = female pin header, 2 pins [form="♀ (female)"]

nets:
  N1: IC1.Vf+, R1.Pin_1, D1.cathode
  N2: IC1.Vf-, R2.Pin_1, D1.anode
  GND/MIDI_IN_GND/MIDI_THRU_GND: IC1.GND, IC3.E7_RC1, IC3.E6_RC0, IC3.E5, IC3.E4, IC3.GND, IC3.E3, IC3.E2, IC3.E1, IC3.E0, IC3.M0, X1.GND, C4.-, J2.pin1, IC4.GND, U1.connector0, U1.connector6, part.GND, U1_1.C1, J8.pin1, J9.pin1, J11.pin2
  MIDI_RX: IC1.Vo, R3.Pin_0, J7.pin1, U1.connector1, U1_1.A1
  5V: IC1.Vcc, R3.Pin_1, IC3.VCC, R4.Pin_1, R8.Pin_0, C4.+, IC4.VCC, U1.connector13, part.VCC, J11.pin1
  MIDI_IN_4: R1.Pin_0, J3.pin1
  MIDI_IN_5: R2.Pin_0, J1.pin1
  SPKJ_TX: IC3.RX, J12.pin2
  SPKJ_RST: IC3.RST, J12.pin1
  N3: IC3.M1, R4.Pin_0
  SPKJ_BHF: IC3.D2_BHF, J10.pin3
  SPKJ_SPK: IC3.D1_SPK, J10.pin2
  SPKJ_RDY: IC3.D0_RDY, J10.pin1
  SPKJ_SND_PWM: IC3.VOICE, J9.pin2
  3.3V: X1.VCC
  µSD_CS: X1.CS
  µSD_MOSI: X1.MOSI
  µSD_CLK: X1.SCK
  µSD_MISO: X1.MISO
  N4: R7.Pin_0, U1.connector2, U1_1.Y1
  MIDI_THRU_5: R7.Pin_1, J6.pin1
  MIDI_THRU_4: R8.Pin_1, J4.pin1
  TTS256_RST: IC4.RST
  TTS256_TX: IC4.RX
  TTS256_WAIT: IC4.SJ_RDY
  TTS256_RX: IC4.SJ_TX

notes:
  Sing'n'Spell, 1.0.0
  MIDI_IN_DIN_5
  MIDI_IN_DIN_4
  MIDI_IN_DIN_GND
  MIDI_THRU_DIN_4
  MIDI_THRU_DIN_5
  MIDI_IN_UART

custom parts:
  6n137 Optocoupler: 6n137 fast Optocoupler. With 8 pins on a 300mil dual inline package (DIP) footprint. Ve is strobe input. Output is inverting.
  SparkFun - microSD Transflash: https://www.sparkfun.com/products/544 Breakout board for the microSD socket that is not much bigger than your fingernail. Compatible with the SPI interface found on any SD card, this tiny form factor was created for cell phone storage and is perfect for your next MP3 project! Board comes fully assembled and tested. The bare socket is available.
  Small signal Diode flat 300mil: Small signal diode such as the 1n4148 Footprint: mounted flat on 300mil centers.
  TTS256: The TTS256 is an 8-bit microprocessor programmed with 600 letter-to-sound rules for the automatic, real-time translation of English text to allophone addresses. Combined with the Magnevation SpeakJet or the Savage Innovations SpeakGin, the TTS256 makes a complete text-to-speech solution.
  74x125: 74x125 quad tristate buffer active low enable. The 74ahc125 variety is useful as a level translator as the inputs are 5V tolorant when run with a VCC of 3.3V (and will thus take a 5V signal in and provide a 3.3V signal out.) As well this part uses schematic subparts so you can drag each of the 4 gates to a different place in schematic view. Note having many (around 10 or more) subpart parts in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
  74x125: 74x125 quad tristate buffer active low enable. The 74ahc125 variety is useful as a level translator as the inputs are 5V tolorant when run with a VCC of 3.3V (and will thus take a 5V signal in and provide a 3.3V signal out.) As well this part uses schematic subparts so you can drag each of the 4 gates to a different place in schematic view. Note having many (around 10 or more) subpart parts in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
  74x125: 74x125 quad tristate buffer active low enable. The 74ahc125 variety is useful as a level translator as the inputs are 5V tolorant when run with a VCC of 3.3V (and will thus take a 5V signal in and provide a 3.3V signal out.) As well this part uses schematic subparts so you can drag each of the 4 gates to a different place in schematic view. Note having many (around 10 or more) subpart parts in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
  74x125: 74x125 quad tristate buffer active low enable. The 74ahc125 variety is useful as a level translator as the inputs are 5V tolorant when run with a VCC of 3.3V (and will thus take a 5V signal in and provide a 3.3V signal out.) As well this part uses schematic subparts so you can drag each of the 4 gates to a different place in schematic view. Note having many (around 10 or more) subpart parts in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
  74x125: 74x125 quad tristate buffer active low enable. The 74ahc125 variety is useful as a level translator as the inputs are 5V tolorant when run with a VCC of 3.3V (and will thus take a 5V signal in and provide a 3.3V signal out.) As well this part uses schematic subparts so you can drag each of the 4 gates to a different place in schematic view. Note having many (around 10 or more) subpart parts in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
  74x125: 74x125 quad tristate buffer active low enable. The 74ahc125 variety is useful as a level translator as the inputs are 5V tolorant when run with a VCC of 3.3V (and will thus take a 5V signal in and provide a 3.3V signal out.) As well this part uses schematic subparts so you can drag each of the 4 gates to a different place in schematic view. Note having many (around 10 or more) subpart parts in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
